# Fritzing sketch diagram (saved by Fritzing 0.9.0b)
breadboards: 1

parts:
  Part1 = Arduino Uno (Rev3)
  RHT1 = Humidity and Temperature Sensor RHT03

nets:
  N1: Part1.D2, RHT1.Data-signal

notes:
  dht11 module
  HC-SR04 module
  (not pictured)
